# Fritzing sketch cat_laser_sans_pca_v2 (saved by Fritzing 0.9.6b)
breadboards: 1

parts:
  R3 = Resistor [tolerance=±5% power=0.25 resistance=220 package=THT]  # not connected
  S1 = Pushbutton [package=THT]  # not connected
  Part1 = Arduino Nano (Rev3.0)  # not connected
  R4 = Trimmer Potentiometer [maximum_resistance=10kΩ package=THT]
  R5 = Trimmer Potentiometer [maximum_resistance=10kΩ package=THT]

nets:
  N1: R4.leg1, R5.leg1
